# Fritzing sketch Project Part 1 (saved by Fritzing 0.9.3b)
breadboards: 1

parts:
  Part1 = Arduino Uno (Rev3)
  LCD1 = LCD screen
  R1 = Trimmer Potentiometer [maximum_resistance=10kΩ package=THT]
  R2 = Resistor [tolerance=±5% resistance=220 package=THT]
  R3 = Resistor [tolerance=±5% resistance=220 package=THT]
  LED1 = LED - 5mm [color="Red (633nm)" package="5 mm [THT]"]
  LED2 = LED - 5mm [color="Red (633nm)" package="5 mm [THT]"]
  SEN1 = Pulse Sensor [package=SIP]

nets:
  N1: Part1.A0, SEN1.Signal
  N2: Part1.D8, LED2.anode
  N3: Part1.D11_PWM/MOSI, LCD1.DB3
  N4: Part1.D12/MISO, LCD1.RS
  N5: Part1.D13/SCK, LED1.cathode
  N6: Part1.D2, LCD1.DB7
  N7: Part1.D3_PWM, LCD1.DB6
  N8: Part1.D4, LCD1.DB5
  N9: Part1.D5_PWM, LCD1.DB4
  5V: Part1.5V, LCD1.VDD, LCD1.LED+, R1.leg1, R2.Pin_1, R3.Pin_1, SEN1.Vcc
  GND: Part1.GND, LCD1.VSS, LCD1.R/W, LCD1.LED-, R1.leg2, SEN1.GND
  N10: LCD1.V0, R1.wiper
  N11: R2.Pin_0, LED2.cathode
  N12: R3.Pin_0, LED1.anode

custom parts:
  Pulse Sensor: Pulse Sensor Optical Heart Rate Monitor for Arduino and other microcontrollers
