# Fritzing sketch Final Project Fritizing Diagram (saved by Fritzing 0.9.3b)
breadboards: 1

parts:
  Part1 = Arduino Uno (Rev3)
  LCD1 = LCD screen
  R1 = Trimmer Potentiometer [maximum_resistance=10kΩ package=THT]
  R2 = Resistor [tolerance=±5% resistance=220 package=THT]
  R3 = Resistor [tolerance=±5% resistance=220 package=THT]
  LED1 = LED - 5mm [color="Red (633nm)" package="5 mm [THT]"]
  LED2 = LED - 5mm [color="Red (633nm)" package="5 mm [THT]"]
  SEN1 = Pulse Sensor [package=SIP]
  Part2 = BME280 Breakout
  U1 = DS1307 [package=so08]

nets:
  N1: Part1.A0, SEN1.Signal
  N2: Part1.A4/SDA, Part2.SDI/SDA, U1.SDA
  N3: Part1.A5/SCL, Part2.SCK/SCL, U1.SCL
  N4: Part1.D8, LED2.anode
  N5: Part1.D11_PWM/MOSI, LCD1.DB3
  N6: Part1.D12/MISO, LCD1.RS
  N7: Part1.D13/SCK, LED1.cathode
  N8: Part1.D2, LCD1.DB7
  N9: Part1.D3_PWM, LCD1.DB6
  N10: Part1.D4, LCD1.DB5
  N11: Part1.D5_PWM, LCD1.DB4
  VCC: Part1.5V, LCD1.VDD, LCD1.LED+, R1.leg1, R2.Pin_1, R3.Pin_1, SEN1.Vcc, Part2.3.3V, U1.VCC
  GND: Part1.GND, LCD1.VSS, LCD1.R/W, LCD1.LED-, R1.leg2, SEN1.GND, Part2.GND, U1.GND
  N12: LCD1.V0, R1.wiper
  N13: R2.Pin_0, LED2.cathode
  N14: R3.Pin_0, LED1.anode

custom parts:
  Pulse Sensor: Pulse Sensor Optical Heart Rate Monitor for Arduino and other microcontrollers
